// Logisim project CPU.circ as structural Verilog: 5 circuits, main circuit Logic_Unit
module Logic_Unit (
  input  [7:0] a,
  input  [7:0] b,
  input  [1:0] f,
  output [7:0] y
);

  wire [7:0] and_1_out, not_1_out, or_1_out, xor_1_out;

  assign not_1_out = ~a;  // NOT_Gate not_1, 8 bits wide
  assign and_1_out = a & b;  // AND_Gate and_1, 8 bits wide
  assign or_1_out = a | b;  // OR_Gate or_1, 8 bits wide
  assign xor_1_out = a ^ b;  // XOR_Gate xor_1, 8 bits wide
  Multiplexer #(.select(2), .width(8), .enable("false")) multiplexer_1 (
    .in0(not_1_out), .in1(and_1_out), .in2(or_1_out), .in3(xor_1_out), .out(y), .sel(f));
endmodule

module Arithmetic_Unit (
  input  [7:0] a,
  input  [7:0] b,
  input  [1:0] f,
  output [7:0] y
);

  wire [7:0] adder_1_out, divider_1_out, multiplier_1_out, subtractor_1_out;

  Adder adder_1 (.a(a), .b(b), .out(adder_1_out));  // open: cin, cout
  Subtractor subtractor_1 (.a(a), .b(b), .out(subtractor_1_out));  // open: bin, bout
  Multiplier multiplier_1 (.a(a), .b(b), .out(multiplier_1_out));  // open: cin, cout
  Divider divider_1 (.a(a), .b(b), .out(divider_1_out));  // open: upper, rem
  Multiplexer #(.select(2), .width(8), .enable("false")) multiplexer_1 (
    .in0(adder_1_out), .in1(subtractor_1_out), .in2(multiplier_1_out), .in3(divider_1_out), .out(y), .sel(f));
endmodule

module ALU (
  input  [7:0] ra,
  input  [7:0] rb_or_imm,
  input  [3:0] alufn,
  output [7:0] alu_out,
  output Z,
  output N
);

  wire [7:0] arithmetic_unit_1_y, logic_unit_1_y, multiplexer_1_out, multiplexer_2_out, not_1_out, not_2_out;

  assign not_1_out = ~ra;  // NOT_Gate not_1, 8 bits wide
  assign not_2_out = ~rb_or_imm;  // NOT_Gate not_2, 8 bits wide
  Multiplexer #(.width(8), .enable("false")) multiplexer_1 (
    .in0(ra), .in1(not_1_out), .out(multiplexer_1_out), .sel(alufn[0]));
  Multiplexer #(.width(8), .enable("false")) multiplexer_2 (
    .in0(rb_or_imm), .in1(not_2_out), .out(multiplexer_2_out), .sel(alufn[1]));
  Arithmetic_Unit arithmetic_unit_1 (
    .a(multiplexer_1_out), .b(multiplexer_2_out), .f({alufn[2], alufn[0]}), .y(arithmetic_unit_1_y));
  Logic_Unit logic_unit_1 (.a(ra), .b(multiplexer_2_out), .f({alufn[2], alufn[0]}), .y(logic_unit_1_y));
  Multiplexer #(.width(8), .enable("false")) multiplexer_3 (
    .in0(arithmetic_unit_1_y), .in1(logic_unit_1_y), .out(alu_out), .sel(alufn[3]));
  nor nor_1 (Z, alu_out[0], alu_out[1], alu_out[2], alu_out[3], alu_out[4], alu_out[5], alu_out[6], alu_out[7]);

  assign N = alu_out[7];
endmodule

module Register_File (
  input  clk,
  input  [7:0] in_value,
  input  RegWrite,
  input  [2:0] Ra,
  input  [2:0] Rd,
  input  [2:0] Rb,
  output [7:0] out_a,
  output [7:0] out_b
);

  wire demultiplexer_1_out0, demultiplexer_1_out1, demultiplexer_1_out2, demultiplexer_1_out3,
       demultiplexer_1_out4, demultiplexer_1_out5, demultiplexer_1_out6, demultiplexer_1_out7;
  wire [7:0] R0_q, R1_q, R2_q, R3_q, R4_q, R5_q, R6_q, R7_q;

  Demultiplexer #(.select(3), .enable("false")) demultiplexer_1 (
    .out0(demultiplexer_1_out0), .out1(demultiplexer_1_out1), .out2(demultiplexer_1_out2),
    .out3(demultiplexer_1_out3), .out4(demultiplexer_1_out4), .out5(demultiplexer_1_out5),
    .out6(demultiplexer_1_out6), .out7(demultiplexer_1_out7), .in(RegWrite), .sel(Rd));
  Register R0 (.D(in_value), .en(demultiplexer_1_out0), .clk(clk), .Q(R0_q));  // open: clr
  Register R1 (.D(in_value), .en(demultiplexer_1_out1), .clk(clk), .Q(R1_q));  // open: clr
  Register R2 (.D(in_value), .en(demultiplexer_1_out2), .clk(clk), .Q(R2_q));  // open: clr
  Register R3 (.D(in_value), .en(demultiplexer_1_out3), .clk(clk), .Q(R3_q));  // open: clr
  Register R4 (.D(in_value), .en(demultiplexer_1_out4), .clk(clk), .Q(R4_q));  // open: clr
  Register R5 (.D(in_value), .en(demultiplexer_1_out5), .clk(clk), .Q(R5_q));  // open: clr
  Register R6 (.D(in_value), .en(demultiplexer_1_out6), .clk(clk), .Q(R6_q));  // open: clr
  Register R7 (.D(in_value), .en(demultiplexer_1_out7), .clk(clk), .Q(R7_q));  // open: clr
  Multiplexer #(.select(3), .width(8), .enable("false")) multiplexer_1 (
    .in0(R0_q), .in1(R1_q), .in2(R2_q), .in3(R3_q), .in4(R4_q), .in5(R5_q), .in6(R6_q), .in7(R7_q),
    .out(out_a), .sel(Ra));
  Multiplexer #(.select(3), .width(8), .enable("false")) multiplexer_2 (
    .in0(R0_q), .in1(R1_q), .in2(R2_q), .in3(R3_q), .in4(R4_q), .in5(R5_q), .in6(R6_q), .in7(R7_q),
    .out(out_b), .sel(Rb));
endmodule

module CPU (
);

  wire clk, Data, Load, LoadL, or_1_out, or_2_out, Store;
  wire [1:0] alu_1_z;
  wire [2:0] controlled_buffer_5_out, Rb;
  wire [7:0] alu_1_alu_out, controlled_buffer_2_out, ram_1_data, register_file_1_out_a, register_file_1_out_b;
  wire [9:0] Addr, counter_1_q;
  wire [15:0] rom_1_data;
  wire [15:13] Instruction_Register_q;

  Counter #(.width(10), .max('h3ff)) counter_1 (.clk(clk), .Q(counter_1_q));  // open: clr, load, up, count, D, carry
  Clock u_clk (.out(clk));
  RAM #(.addrWidth(10)) ram_1 (.addr(Addr), .we(Store), .oe(Load), .clk(clk), .data(ram_1_data));
  ROM #(.addrWidth(10), .dataWidth(16)) rom_1 (.addr(counter_1_q), .data(rom_1_data));
  or or_1 (or_1_out, LoadL, Load);
  Controlled_Buffer controlled_buffer_1 ();  // open: in, out, en
  assign controlled_buffer_2_out = Data ? alu_1_alu_out : 8'bz;  // Controlled_Buffer controlled_buffer_2
  assign controlled_buffer_2_out = Load ? ram_1_data : 8'bz;  // Controlled_Buffer controlled_buffer_3
  assign controlled_buffer_2_out = LoadL ? Addr[7:0] : 8'bz;  // Controlled_Buffer controlled_buffer_4
  assign controlled_buffer_5_out = or_1_out ? Rb : 3'bz;  // Controlled_Buffer controlled_buffer_5
  assign controlled_buffer_5_out = Data ? Addr[5:3] : 3'bz;  // Controlled_Buffer controlled_buffer_6
  or or_2 (or_2_out, Data, Load, LoadL);
  Register #(.width(16)) Instruction_Register (
    .D(rom_1_data), .clk(clk), .Q({Instruction_Register_q, Addr, Rb}));  // open: en, clr
  assign ram_1_data = Store ? register_file_1_out_b : 8'bz;  // Controlled_Buffer controlled_buffer_7
  Register_File register_file_1 (
    .clk(clk), .in_value(controlled_buffer_2_out), .RegWrite(or_2_out), .Ra(Addr[2:0]),
    .Rd(controlled_buffer_5_out), .Rb(Rb), .out_a(register_file_1_out_a), .out_b(register_file_1_out_b));
  and and_1 (Data, ~Instruction_Register_q[15], ~Instruction_Register_q[14], Instruction_Register_q[13]);  // AND_Gate
  and and_2 (Load, ~Instruction_Register_q[15], Instruction_Register_q[14], ~Instruction_Register_q[13]);  // AND_Gate
  and and_3 (Store, Instruction_Register_q[15], ~Instruction_Register_q[14], ~Instruction_Register_q[13]);  // AND_Gate
  and and_4 (LoadL, ~Instruction_Register_q[15], Instruction_Register_q[14], Instruction_Register_q[13]);  // AND_Gate
  ALU alu_1 (
    .ra(register_file_1_out_a), .rb_or_imm(register_file_1_out_b), .alufn(Addr[9:6]),
    .alu_out(alu_1_alu_out), .Z(alu_1_z[0]), .N(alu_1_z[1]));
  Register #(.width(2)) Status_Register (.D(alu_1_z), .en(Data), .clk(clk));  // open: Q, clr

  // Other names for the same wires on the sheet: Ra[2:0] = Addr[2:0]; Value[7:0] = Addr[7:0]; Rd[2:0] = Addr[5:3];
  //   op[3:0] = Addr[9:6]

  // Notes on the sheet:
  //   System Clock
  //   Program Counter
  //   Data Memory
  //   contents of rom_1 (hex, n*v repeats v):
  //   601c 6016 2066 8039
  //   Instruction Memory
  //   Instruction Decoder
  //   Control Unit
  //   Instruction Set
  //   op Rd, Ra, Rb (Rd = Ra op Rb)
  //   LDR Rd, =N [0110 0NNN NNNN NRRR]
  //   LDR Rd, [A] [010A AAAA AAAA ARRR]
  //   STR Rs, [A] [100A AAAA AAAA ARRR]
  //   op Rd, Ra, Rb [001o oood ddaa abbb]
  //   LDR Rd, =N (load 8-bit literal value into register Rd)
  //   Instruction Format
  //   LDR Rd, [A] (load value from RAM at 10-bit address A into register Rd)
  //   STR Rs, [A] (store value in register Rs in RAM at 10-bit address A)
endmodule
